# Fritzing sketch Button_push_on (saved by Fritzing 1.0.6)
breadboards: 1

parts:
  A1 = Arduino UNO R4 WiFi
  S1 = Pushbutton [package="[THT]"]
  R1 = Resistor [tolerance=±5% power=0.25W resistance=220 package=THT]

nets:
  N1: A1.Pin_8, A1.Pin_27, S1.Pin_3, S1.Pin_4
  N2: A1.Pin_9, A1.Pin_30, R1.Pin_0
  N3: A1.Pin_36, S1.Pin_1, S1.Pin_2, R1.Pin_1

custom parts:
  Arduino UNO R4 WiFi: The Arduino UNO R4 WiFi merges the RA4M1 microprocessor from Renesas with the ESP32-S3 from Espressif, creating an all-in-one tool for makers with enhanced processing power and a diverse array of new peripherals.
