# Fritzing sketch LED_matrix_8x8 (saved by Fritzing 1.0.6)

parts:
  A1 = Arduino UNO R4 WiFi
  Part1 = NeoPixel NeoMatrix 8x8 [part_number=1487]

nets:
  N1: A1.Pin_8, A1.Pin_27, Part1.VDD
  N2: A1.Pin_9, A1.Pin_48, Part1.GND
  N3: A1.Pin_40, Part1.IN

custom parts:
  Arduino UNO R4 WiFi: The Arduino UNO R4 WiFi merges the RA4M1 microprocessor from Renesas with the ESP32-S3 from Espressif, creating an all-in-one tool for makers with enhanced processing power and a diverse array of new peripherals.
  NeoPixel NeoMatrix 8x8: Put on your sunglasses before wiring up this LED matrix - 64 eye-blistering RGB LEDs adorn the NeoMatrix for a blast of configurable color. Arranged in an 8x8 matrix, each pixel is individually addressable. Only one microcontroller pin is required to control all the LEDs, and you get 24 bit color for each LED.
