# Fritzing sketch LED_matrix_ring_12 (saved by Fritzing 1.0.6)

parts:
  A1 = Arduino UNO R4 WiFi
  Part2 = 12 NeoPixel Ring [part_number=1643]

nets:
  N1: A1.Pin_8, A1.Pin_27, Part2.VDD
  N2: A1.Pin_9, A1.Pin_18, A1.Pin_25, Part2.GND
  N3: A1.Pin_40, Part2.IN

custom parts:
  Arduino UNO R4 WiFi: The Arduino UNO R4 WiFi merges the RA4M1 microprocessor from Renesas with the ESP32-S3 from Espressif, creating an all-in-one tool for makers with enhanced processing power and a diverse array of new peripherals.
  12 NeoPixel Ring: 12 ultra bright smart LED NeoPixels are arranged in a circle with 1.5" (37mm) outer diameter. The rings are 'chainable' - connect the output pin of one to the input pin of another. Use only one microcontroller pin to control as many as you can chain together! Each LED is addressable as the driver chip is inside the LED. Each one has ~18mA constant current drive so the color will be very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
